# Fritzing sketch Circuit (saved by Fritzing 0.9.3b)
circuit board: 8.46667cm x 5.64444cm
breadboards: 1

parts:
  Pololu_A1 = Pololu A4988 [package=SO16]
  Part1 = Arduino Uno (Rev3) - ICSP
  Pololu_A2 = Pololu A4988 [package=SO16]
  M1 = Stepper Motor - Unipolar
  M2 = Stepper Motor - Unipolar
  C1 = Electrolytic Capacitor [capacitance=47µF package="0605 [SMD, electrolytic]"]
  C2 = Electrolytic Capacitor [capacitance=47µF package="0605 [SMD, electrolytic]"]
  VCC1 = Battery block 9V

nets:
  N1: Pololu_A1.RESET, Pololu_A1.SLEEP
  N2: Pololu_A1.STEP, Part1.D10_PWM/SS
  N3: Pololu_A1.DIR, Part1.D11_PWM/MOSI
  N4: Pololu_A1.GND#8, Part1.GND, Pololu_A2.GND#8
  VDD: Pololu_A1.VDD, Part1.5V, Pololu_A2.VDD
  N5: Pololu_A1.1B, M1.D
  N6: Pololu_A1.1A, M1.B
  N7: Pololu_A1.2A, M1.C
  N8: Pololu_A1.2B, M1.A
  N9: Pololu_A1.GND#14, Pololu_A2.GND#14, C1.-, C2.-, VCC1.-
  N10: Pololu_A1.VMOT, Pololu_A2.VMOT, C1.+, C2.+, VCC1.+
  N11: Part1.D8, Pololu_A2.STEP
  N12: Part1.D9_PWM, Pololu_A2.DIR
  N13: Pololu_A2.RESET, Pololu_A2.SLEEP
  N14: Pololu_A2.1B, M2.D
  N15: Pololu_A2.1A, M2.B
  N16: Pololu_A2.2A, M2.C
  N17: Pololu_A2.2B, M2.A

notes:
  12V bettery or 10V bettery
